# Fritzing sketch moti_2 (saved by Fritzing 0.7.12b)

parts:
  U1 = Arduino Mega
  Composants1 = IMU Digital Combo Board 6DOF
  LED2 = Super Flux RGB LED (com. anode)

nets:
  3V3: U1.3V3, Composants1.3.3V
  N1: U1.A4, Composants1.SCL
  N2: U1.A5, Composants1.SDA
  N3: U1.D44, LED2.red_cathode
  N4: U1.D45, LED2.green_cathode
  N5: U1.D46, LED2.blue_cathode
  GND: U1.GND, Composants1.GND, LED2.common_anode
