# Fritzing sketch global (saved by Fritzing 0.7.12b)
breadboards: 1

parts:
  U1 = Arduino Mega
  Composants3 = Arduino Motor Shield  # not connected
  Composants4 = Breakout Board for Electret Microphone

nets:
  GND: U1.GND, Composants4.GND
  3V3: U1.3V3, Composants4.VCC
  N1: U1.A8, Composants4.AUD
