# Fritzing sketch moti (saved by Fritzing 0.7.12b)
breadboards: 1

parts:
  Composants3 = Arduino Motor Shield
  Arduino1 = Arduino
  VCC1 = 4 x AAA Battery Mount
  VCC2 = 4 x AAA Battery Mount
  M1 = DC Motor
  M2 = DC Motor
  Composants5 = Breakout Board for Electret Microphone
  Composants6 = Triple Axis Accelerometer Breakout - ADXL335
  LED1 = Red LED - 5mm
  LED2 = Blue smd LED [package="0805 [SMD]"]
  LED3 = green smd LED [package="1206 [SMD]"]
  R1 = 2.2k Ω Resistor [package=THT]
  R2 = 2.2k Ω Resistor [package=THT]
  R4 = 2.2k Ω Resistor [package=THT]

nets:
  N1: Composants3.GND, VCC2.-
  N2: Composants3.VIN, VCC2.+
  N3: Composants3.OUT3, M2.pin_2
  N4: Composants3.OUT4, M2.pin_1
  N5: Composants3.OUT2, M1.pin_2
  N6: Composants3.OUT1, M1.pin_1
  N7: Composants3.D4, Arduino1.D4
  N8: Composants3.D5, Arduino1.D5
  N9: Composants3.D6, Arduino1.D6
  N10: Composants3.D7, Arduino1.D7
  GND: Arduino1.GND, VCC1.-, Composants5.GND, Composants6.GND, LED1.cathode, LED2.cathode, LED3.cathode
  N11: Arduino1.D10, R2.Pin_0
  N12: Arduino1.D9, R1.Pin_0
  N13: Arduino1.D8, R4.Pin_0
  VCC: Arduino1.3V3, Composants5.VCC, Composants6.VCC
  N14: Arduino1.+5V, VCC1.+
  N15: Arduino1.A0, Composants6.XOUT
  N16: Arduino1.A2, Composants6.ZOUT
  N17: Arduino1.A3, Composants5.AUD
  N18: LED1.anode, R2.Pin_1
  N19: LED2.anode, R1.Pin_1
  N20: LED3.anode, R4.Pin_1
