# Fritzing sketch moti_1 (saved by Fritzing 0.7.12b)
breadboards: 1

parts:
  Composants3 = Arduino Motor Shield
  Arduino1 = Arduino
  Composants7 = NCP1400 Step-Up Breakout
  VCC1 = 4 x AAA Battery Mount
  VCC2 = 4 x AAA Battery Mount
  Composants8 = Triple Axis Accelerometer Breakout - ADXL335
  Composants9 = Breakout Board for Electret Microphone
  M1 = DC Motor
  M2 = DC Motor
  LED2 = smd LED [color="Red (633nm)" package="1206 [SMD]"]
  R2 = 2.2k Ω Resistor [package=THT]
  R3 = 2.2k Ω Resistor [package=THT]
  R4 = 2.2k Ω Resistor [package=THT]
  LED3 = smd LED [color="Red (633nm)" package="1206 [SMD]"]
  LED4 = smd LED [color="Red (633nm)" package="1206 [SMD]"]

nets:
  GND: Composants3.GND, Arduino1.GND, Composants7.GND, VCC1.-, VCC2.-, Composants8.GND, Composants9.GND, LED2.cathode, LED3.cathode, LED4.cathode
  N1: Composants3.VIN, Composants7.VOUT
  N2: Composants3.OUT3, M1.pin_2
  N3: Composants3.OUT4, M1.pin_1
  N4: Composants3.OUT2, M2.pin_2
  N5: Composants3.OUT1, M2.pin_1
  VCC: Composants3.3.3V, Composants3.AREF, Composants8.VCC, Composants9.VCC
  5V: Composants3.5V, Arduino1.+5V, VCC1.+
  N6: Composants3.A0, Composants8.XOUT
  N7: Composants3.A1, Composants8.YOUT
  N8: Composants3.A2, Composants8.ZOUT
  N9: Composants3.A3, Composants9.AUD
  N10: Composants3.D4, Arduino1.D4
  N11: Composants3.D5, Arduino1.D5
  N12: Composants3.D6, Arduino1.D6
  N13: Composants3.D7, Arduino1.D7
  N14: Composants3.D8, LED2.anode, R3.Pin_0, R3.Pin_1
  N15: Composants3.D9, R4.Pin_0, R4.Pin_1, LED3.anode
  N16: Composants3.D10, R2.Pin_0, R2.Pin_1, LED4.anode
  N17: Composants7.VIN, VCC2.+
